// Logisim project 4bit-adder.circ as structural Verilog: 2 circuits, main circuit main
module main (
  input  in_1,
  input  in_2,
  input  in_3,
  input  in_4,
  input  in_5,
  input  in_6,
  input  in_7,
  input  in_8,
  input  in_9,
  output out_10,
  output out_11,
  output out_12,
  output out_13,
  output out_14
);

  wire full_adder_1_cout, full_adder_2_cout, full_adder_3_cout;

  full_adder full_adder_1 (.A(in_8), .B(in_4), .Cin(in_9), .SUM(out_10), .Cout(full_adder_1_cout));
  full_adder full_adder_2 (.A(in_7), .B(in_3), .Cin(full_adder_1_cout), .SUM(out_11), .Cout(full_adder_2_cout));
  full_adder full_adder_3 (.A(in_6), .B(in_2), .Cin(full_adder_2_cout), .SUM(out_12), .Cout(full_adder_3_cout));
  full_adder full_adder_4 (.A(in_5), .B(in_1), .Cin(full_adder_3_cout), .SUM(out_13), .Cout(out_14));
endmodule

module full_adder (
  input  A,
  input  B,
  input  Cin,
  output SUM,
  output Cout
);

  wire and_1_out, and_2_out, xor_1_out;

  xor xor_1 (xor_1_out, A, B);
  xor xor_2 (SUM, xor_1_out, Cin);
  and and_1 (and_1_out, Cin, xor_1_out);
  and and_2 (and_2_out, A, B);
  or or_1 (Cout, and_1_out, and_2_out);
endmodule
