// Logisim project CMOS Full Adder.circ as structural Verilog: 3 circuits, main circuit Transistor
module Transistor (
  input  A,
  input  B,
  input  Cin,
  output SUM,
  output Cout
);

  wire transistor_1_out, transistor_3_out, transistor_5_out, transistor_6_out, transistor_8_out,
       transistor_9_out, transistor_10_out, transistor_14_out, transistor_15_out, transistor_17_out,
       transistor_19_out, transistor_21_out, transistor_23_out, transistor_24_out, transistor_26_out,
       transistor_29_out, transistor_32_out, transistor_33_out, transistor_35_out, transistor_37_out,
       transistor_40_out, transistor_43_out;

  Transistor_part transistor_1 (.in(1'b1), .out(transistor_1_out), .gate(A));
  Transistor_part #(.\type ("n")) transistor_2 (.in(1'b0), .out(transistor_1_out), .gate(A));
  Transistor_part transistor_3 (.in(1'b1), .out(transistor_3_out), .gate(B));
  Transistor_part #(.\type ("n")) transistor_4 (.in(1'b0), .out(transistor_3_out), .gate(B));
  Transistor_part transistor_5 (.in(1'b1), .out(transistor_5_out), .gate(transistor_3_out));
  Transistor_part transistor_6 (.in(transistor_5_out), .out(transistor_6_out), .gate(transistor_1_out));
  Transistor_part #(.\type ("n")) transistor_7 (.in(1'b0), .out(transistor_6_out), .gate(transistor_1_out));
  Transistor_part transistor_8 (.in(1'b1), .out(transistor_8_out), .gate(transistor_1_out));
  Transistor_part transistor_9 (.in(1'b1), .out(transistor_9_out), .gate(A));
  Transistor_part transistor_10 (.in(transistor_8_out), .out(transistor_10_out), .gate(B));
  Transistor_part transistor_11 (.in(transistor_9_out), .out(transistor_10_out), .gate(transistor_3_out));
  Transistor_part #(.\type ("n")) transistor_12 (
    .in(transistor_14_out), .out(transistor_10_out), .gate(transistor_1_out));
  Transistor_part #(.\type ("n")) transistor_13 (.in(transistor_15_out), .out(transistor_10_out), .gate(A));
  Transistor_part #(.\type ("n")) transistor_14 (.in(1'b0), .out(transistor_14_out), .gate(transistor_3_out));
  Transistor_part #(.\type ("n")) transistor_15 (.in(1'b0), .out(transistor_15_out), .gate(B));
  Transistor_part #(.\type ("n")) transistor_16 (.in(1'b0), .out(transistor_6_out), .gate(transistor_3_out));
  Transistor_part transistor_17 (.in(1'b1), .out(transistor_17_out), .gate(transistor_10_out));
  Transistor_part #(.\type ("n")) transistor_18 (.in(1'b0), .out(transistor_17_out), .gate(transistor_10_out));
  Transistor_part transistor_19 (.in(1'b1), .out(transistor_19_out), .gate(transistor_10_out));
  Transistor_part #(.\type ("n")) transistor_20 (.in(1'b0), .out(transistor_19_out), .gate(transistor_10_out));
  Transistor_part transistor_21 (.in(1'b1), .out(transistor_21_out), .gate(Cin));
  Transistor_part #(.\type ("n")) transistor_22 (.in(1'b0), .out(transistor_21_out), .gate(Cin));
  Transistor_part transistor_23 (.in(1'b1), .out(transistor_23_out), .gate(transistor_17_out));
  Transistor_part transistor_24 (.in(transistor_23_out), .out(transistor_24_out), .gate(transistor_26_out));
  Transistor_part #(.\type ("n")) transistor_25 (.in(1'b0), .out(transistor_24_out), .gate(transistor_26_out));
  Transistor_part transistor_26 (.in(1'b1), .out(transistor_26_out), .gate(Cin));
  Transistor_part #(.\type ("n")) transistor_27 (.in(1'b0), .out(transistor_26_out), .gate(Cin));
  Transistor_part #(.\type ("n")) transistor_28 (.in(1'b0), .out(transistor_24_out), .gate(transistor_17_out));
  Transistor_part transistor_29 (.in(1'b1), .out(transistor_29_out), .gate(transistor_10_out));
  Transistor_part transistor_30 (.in(transistor_29_out), .out(SUM), .gate(transistor_21_out));
  Transistor_part #(.\type ("n")) transistor_31 (.in(transistor_32_out), .out(SUM), .gate(transistor_10_out));
  Transistor_part #(.\type ("n")) transistor_32 (.in(1'b0), .out(transistor_32_out), .gate(Cin));
  Transistor_part transistor_33 (.in(1'b1), .out(transistor_33_out), .gate(transistor_24_out));
  Transistor_part #(.\type ("n")) transistor_34 (.in(1'b0), .out(transistor_33_out), .gate(transistor_24_out));
  Transistor_part transistor_35 (.in(1'b1), .out(transistor_35_out), .gate(transistor_6_out));
  Transistor_part #(.\type ("n")) transistor_36 (.in(1'b0), .out(transistor_35_out), .gate(transistor_6_out));
  Transistor_part transistor_37 (.in(1'b1), .out(transistor_37_out), .gate(transistor_19_out));
  Transistor_part transistor_38 (.in(transistor_37_out), .out(SUM), .gate(Cin));
  Transistor_part #(.\type ("n")) transistor_39 (.in(transistor_40_out), .out(SUM), .gate(transistor_19_out));
  Transistor_part #(.\type ("n")) transistor_40 (.in(1'b0), .out(transistor_40_out), .gate(transistor_21_out));
  Transistor_part transistor_41 (.in(1'b1), .out(Cout), .gate(transistor_33_out));
  Transistor_part #(.\type ("n")) transistor_42 (.in(transistor_43_out), .out(Cout), .gate(transistor_33_out));
  Transistor_part #(.\type ("n")) transistor_43 (.in(1'b0), .out(transistor_43_out), .gate(transistor_35_out));
  Transistor_part transistor_44 (.in(1'b1), .out(Cout), .gate(transistor_35_out));

  // Notes on the sheet:
  //   NOT GATE
  //   NOT GATE
  //   FULL ADDER CIRCUIT - TRANSISTOR (CMOS)
  //   NOT A
  //   NOT B
  //   reference: https://www.elprocus.com/half-adder-and-full-adder/
  //   XOR
  //   A XOR B
  //   NOT B
  //   NOT A
  //   NOT B
  //   NOT A
  //   NAND
  //   Inputting NOT A and NOT B results to A AND B
  //   A XOR B
  //   A AND B
  //   A XOR B
  //   NOT GATE
  //   Cin
  //   NOT GATE
  //   NOT GATE
  //   NOT GATE
  //   SUM COMPUTATION
  //   XOR
  //   Cin XOR (A XOR B)
  //   Cin AND (A XOR B)
  //   NAND
  //   Inputting NOT Cin and NOT (A XOR B) results to Cin AND (A XOR B)
  //   CARRY OUT COMPUTATION
  //   NOT GATE
  //   NOT GATE
  //   A XOR B XOR Cin
  //   NOR
  //   (Cin AND (A XOR B)) OR (A AND B)
  //   Inputting NOT (A AND B) and NOT (Cin AND (A XOR B))
  //   results to (Cin AND (A XOR B)) OR (A AND B)
endmodule

module Logic (
  input  A,
  input  B,
  input  Cin,
  output SUM,
  output Cout
);

  wire and_1_out, and_2_out, xor_1_out;

  xor xor_1 (xor_1_out, A, B);
  xor xor_2 (SUM, xor_1_out, Cin);
  and and_1 (and_1_out, xor_1_out, Cin);
  and and_2 (and_2_out, A, B);
  or or_1 (Cout, and_1_out, and_2_out);

  // Notes on the sheet:
  //   FULL ADDER CIRCUIT - LOGIC
  //   reference: https://www.elprocus.com/half-adder-and-full-adder/
  //   A XOR B XOR Cin
  //   Cin AND (A XOR B)
  //   A AND B
  //   (Cin AND (A XOR B)) OR (A AND B)
endmodule

module _2bit_adder (
  input  a1,
  input  a0,
  input  b1,
  input  b0,
  input  cin,
  output s1,
  output s0,
  output cout
);

  wire logic_1_cout;

  Logic logic_1 (.A(a0), .B(b0), .Cin(cin), .SUM(s0), .Cout(logic_1_cout));
  Logic logic_2 (.A(a1), .B(b1), .Cin(logic_1_cout), .SUM(s1), .Cout(cout));
endmodule
