// Logisim project MOD 85 Async Up Counter.circ as structural Verilog: 4 circuits, main circuit main
module main (
);

  wire BCD_to_7_segment_a_2, BCD_to_7_segment_b_2, BCD_to_7_segment_c_2, BCD_to_7_segment_d_2,
       BCD_to_7_segment_e, BCD_to_7_segment_f, BCD_to_7_segment_g, BCDto_7_segment_a_2, BCDto_7_segment_b_2,
       BCDto_7_segment_c_2, BCDto_7_segment_d_2, BCDto_7_segment_e, BCDto_7_segment_f, BCDto_7_segment_g,
       binary_to_BCD_b_2, binary_to_BCD_c_2, binary_to_BCD_d_2, binary_to_BCD_e_2, binary_to_BCD_f_2,
       binary_to_BCD_g_2, binary_to_BCD_h, binary_to_BCD_i, up_counter_lsb, up_counter_msb, up_counter_out_2,
       up_counter_out_3, up_counter_out_4, up_counter_out_5, up_counter_out_6;

  MOD85_async__up_counter up_counter (
    .MSB(up_counter_msb), .out_2(up_counter_out_2), .out_3(up_counter_out_3), .out_4(up_counter_out_4),
    .out_5(up_counter_out_5), .out_6(up_counter_out_6), .LSB(up_counter_lsb));
  _7bin_to_bcd binary_to_BCD (
    .a(up_counter_msb), .b(up_counter_out_2), .c(up_counter_out_3), .d(up_counter_out_4),
    .e(up_counter_out_5), .f(up_counter_out_6), .g(up_counter_lsb), .b_2(binary_to_BCD_b_2),
    .c_2(binary_to_BCD_c_2), .d_2(binary_to_BCD_d_2), .e_2(binary_to_BCD_e_2), .f_2(binary_to_BCD_f_2),
    .g_2(binary_to_BCD_g_2), .h(binary_to_BCD_h), .i(binary_to_BCD_i));  // open: a_2
  bcd_to_7seg BCD_to_7_segment (
    .a(binary_to_BCD_b_2), .b(binary_to_BCD_c_2), .c(binary_to_BCD_d_2), .d(binary_to_BCD_e_2),
    .a_2(BCD_to_7_segment_a_2), .b_2(BCD_to_7_segment_b_2), .c_2(BCD_to_7_segment_c_2),
    .d_2(BCD_to_7_segment_d_2), .e(BCD_to_7_segment_e), .f(BCD_to_7_segment_f), .g(BCD_to_7_segment_g));
  bcd_to_7seg BCDto_7_segment (
    .a(binary_to_BCD_f_2), .b(binary_to_BCD_g_2), .c(binary_to_BCD_h), .d(binary_to_BCD_i),
    .a_2(BCDto_7_segment_a_2), .b_2(BCDto_7_segment_b_2), .c_2(BCDto_7_segment_c_2),
    .d_2(BCDto_7_segment_d_2), .e(BCDto_7_segment_e), .f(BCDto_7_segment_f), .g(BCDto_7_segment_g));
  _7_Segment_Display u_7_segment_display_1 (
    .g(BCD_to_7_segment_g), .f(BCD_to_7_segment_f), .a(BCD_to_7_segment_a_2), .b(BCD_to_7_segment_b_2),
    .e(BCD_to_7_segment_e), .d(BCD_to_7_segment_d_2), .c(BCD_to_7_segment_c_2));  // open: dp
  _7_Segment_Display u_7_segment_display_2 (
    .g(BCDto_7_segment_g), .f(BCDto_7_segment_f), .a(BCDto_7_segment_a_2), .b(BCDto_7_segment_b_2),
    .e(BCDto_7_segment_e), .d(BCDto_7_segment_d_2), .c(BCDto_7_segment_c_2));  // open: dp

  // Notes on the sheet:
  //   with 7-segment display
  //   MOD 85 ASYNCHRONOUS UP COUNTER
  //   Display
  //   Bruce Oliver B. Apos
  //   2014-19859
  //   EE 160 ST-1L
endmodule

module MOD85_async__up_counter (
  output MSB,
  output out_2,
  output out_3,
  output out_4,
  output out_5,
  output out_6,
  output LSB
);

  wire and_1_out, CLK_out, t_ff_1_qn, t_ff_3_qn, t_ff_4_qn, t_ff_5_qn, t_ff_6_qn, t_ff_7_qn;

  and and_1 (and_1_out, MSB, ~out_2, out_3, ~out_4, out_5, ~out_6, LSB);  // AND_Gate
  T_Flip_Flop t_ff_1 (.clk(t_ff_3_qn), .T(1'b1), .Q(out_2), .Qn(t_ff_1_qn), .reset(and_1_out));  // open: preset, en
  T_Flip_Flop t_ff_2 (.clk(t_ff_1_qn), .T(1'b1), .Q(MSB), .reset(and_1_out));  // open: Qn, preset, en
  T_Flip_Flop t_ff_3 (.clk(t_ff_4_qn), .T(1'b1), .Q(out_3), .Qn(t_ff_3_qn), .reset(and_1_out));  // open: preset, en
  T_Flip_Flop t_ff_4 (.clk(t_ff_5_qn), .T(1'b1), .Q(out_4), .Qn(t_ff_4_qn), .reset(and_1_out));  // open: preset, en
  T_Flip_Flop t_ff_5 (.clk(t_ff_6_qn), .T(1'b1), .Q(out_5), .Qn(t_ff_5_qn), .reset(and_1_out));  // open: preset, en
  T_Flip_Flop t_ff_6 (.clk(t_ff_7_qn), .T(1'b1), .Q(out_6), .Qn(t_ff_6_qn), .reset(and_1_out));  // open: preset, en
  T_Flip_Flop t_ff_7 (.clk(CLK_out), .T(1'b1), .Q(LSB), .Qn(t_ff_7_qn), .reset(and_1_out));  // open: preset, en
  Clock CLK (.out(CLK_out));

  // Notes on the sheet:
  //   MOD 85 ASYNCHRONOUS UP COUNTER
  //   a high is triggered, which results to FF reset.
  //   Uses 7 T-Flip Flops with clock connections coming from Q-inverted, which results to up counting.
  //   The AND gate is configured such that when the output from the counter is 1010101 (85)
endmodule

module bcd_to_7seg (
  input  a,
  input  b,
  input  c,
  input  d,
  output a_2,
  output b_2,
  output c_2,
  output d_2,
  output e,
  output f,
  output g
);

  wire and_1_out, and_2_out, and_3_out, and_4_out, and_5_out, and_6_out, and_7_out, and_8_out, and_9_out,
       and_10_out, and_11_out, and_12_out, and_13_out, and_14_out, and_15_out, and_16_out, and_17_out,
       and_18_out, and_19_out, not_1_out, not_2_out, not_3_out, not_4_out, not_5_out, not_6_out, not_7_out,
       not_8_out, not_9_out, not_10_out, not_11_out, not_12_out, not_13_out, not_14_out, not_15_out,
       not_16_out, not_17_out, not_18_out, not_19_out, not_20_out, not_21_out, not_22_out, not_23_out,
       not_24_out;

  not not_1 (not_1_out, b);
  and and_1 (and_1_out, not_1_out, not_2_out);
  not not_2 (not_2_out, d);
  and and_2 (and_2_out, b, d);
  not not_3 (not_3_out, b);
  not not_4 (not_4_out, c);
  and and_3 (and_3_out, not_4_out, not_5_out);
  not not_5 (not_5_out, d);
  and and_4 (and_4_out, c, d);
  not not_6 (not_6_out, b);
  and and_5 (and_5_out, not_6_out, not_7_out);
  not not_7 (not_7_out, c);
  not not_8 (not_8_out, a);
  and and_6 (and_6_out, not_8_out, d);
  not not_9 (not_9_out, a);
  and and_7 (and_7_out, not_9_out, b);
  not not_10 (not_10_out, b);
  and and_8 (and_8_out, not_10_out, not_11_out);
  not not_11 (not_11_out, d);
  not not_12 (not_12_out, b);
  and and_9 (and_9_out, not_12_out, c);
  and and_10 (and_10_out, c, not_13_out);
  not not_13 (not_13_out, d);
  and and_11 (and_11_out, b, not_14_out, d);
  not not_14 (not_14_out, c);
  not not_15 (not_15_out, b);
  and and_12 (and_12_out, not_15_out, not_16_out);
  not not_16 (not_16_out, d);
  and and_13 (and_13_out, c, not_17_out);
  not not_17 (not_17_out, d);
  not not_18 (not_18_out, c);
  and and_14 (and_14_out, not_18_out, not_19_out);
  not not_19 (not_19_out, d);
  and and_15 (and_15_out, b, not_20_out);
  not not_20 (not_20_out, c);
  and and_16 (and_16_out, b, not_21_out);
  not not_21 (not_21_out, d);
  not not_22 (not_22_out, b);
  and and_17 (and_17_out, not_22_out, c);
  and and_18 (and_18_out, b, not_23_out);
  not not_23 (not_23_out, c);
  and and_19 (and_19_out, b, not_24_out);
  not not_24 (not_24_out, d);
  or or_1 (a_2, and_1_out, c, and_2_out, a);
  or or_2 (b_2, not_3_out, and_3_out, and_4_out);
  or or_3 (c_2, and_5_out, and_6_out, and_7_out);
  or or_4 (d_2, and_8_out, and_9_out, and_10_out, and_11_out, a);
  or or_5 (e, and_12_out, and_13_out);
  or or_6 (f, and_14_out, and_15_out, and_16_out, a);
  or or_7 (g, and_17_out, and_18_out, and_19_out, a);
endmodule

module _7bin_to_bcd (
  input  a,
  input  b,
  input  c,
  input  d,
  input  e,
  input  f,
  input  g,
  output a_2,
  output b_2,
  output c_2,
  output d_2,
  output e_2,
  output f_2,
  output g_2,
  output h,
  output i
);

  wire and_1_out, and_2_out, and_3_out, and_4_out, and_5_out, and_6_out, and_7_out, and_8_out, and_9_out,
       and_10_out, and_11_out, and_12_out, and_13_out, and_14_out, and_15_out, and_16_out, and_17_out,
       and_18_out, and_19_out, and_20_out, and_21_out, and_22_out, and_23_out, and_24_out, and_25_out,
       and_26_out, and_27_out, and_28_out, and_29_out, and_30_out, and_31_out, and_32_out, and_33_out,
       and_34_out, and_35_out, and_36_out, and_37_out, and_38_out, and_39_out, and_40_out, and_41_out,
       and_42_out, and_43_out, and_44_out, and_45_out, and_46_out, and_47_out, and_48_out, and_49_out,
       and_50_out, and_51_out, and_52_out, and_53_out, and_54_out, and_55_out, and_56_out, and_57_out,
       and_58_out, and_59_out, and_60_out, and_61_out, and_62_out, and_63_out, and_64_out, and_65_out,
       and_66_out, and_67_out, and_68_out, and_69_out, and_70_out, and_71_out, and_72_out, and_73_out,
       and_74_out, and_75_out, and_76_out, and_77_out, and_78_out, and_79_out, and_80_out, and_81_out,
       and_82_out, and_83_out, and_84_out, and_85_out, and_86_out, and_87_out, and_88_out, and_89_out,
       and_90_out, and_91_out, and_92_out, and_93_out, and_94_out, and_95_out, and_96_out, and_97_out,
       and_98_out, and_99_out, and_100_out, and_101_out, and_102_out, and_103_out, and_104_out, and_105_out,
       and_106_out, and_107_out, and_108_out, and_109_out, and_110_out, and_111_out, and_112_out,
       and_113_out, and_114_out, and_115_out, and_116_out, and_117_out, and_118_out, and_119_out,
       and_120_out, and_121_out, and_122_out, and_123_out, and_124_out, and_125_out, and_126_out,
       and_127_out, and_128_out, and_129_out, and_130_out, and_131_out, and_132_out, and_133_out,
       and_134_out, and_135_out, and_136_out, and_137_out, and_138_out, and_139_out, and_140_out,
       and_141_out, and_142_out, and_143_out, and_144_out, and_145_out, and_146_out, and_147_out,
       and_148_out, and_149_out, and_150_out, and_151_out, and_153_out, and_154_out, and_155_out,
       and_156_out, and_157_out, and_158_out, and_159_out, and_160_out, and_161_out, and_162_out,
       and_163_out, and_164_out, and_165_out, and_166_out, and_167_out, and_168_out, and_169_out,
       and_170_out, and_171_out, and_172_out, and_173_out, and_174_out, and_175_out, and_176_out,
       and_177_out, and_178_out, and_179_out, and_180_out, and_181_out, and_182_out, and_183_out,
       and_184_out, and_185_out, and_186_out, and_187_out, and_188_out, and_189_out, and_190_out,
       and_191_out, and_192_out, and_193_out, and_194_out, and_195_out, and_196_out, and_197_out,
       and_198_out, and_199_out, and_200_out, and_201_out, and_202_out, and_203_out, and_204_out,
       and_205_out, and_206_out, and_207_out, and_208_out, and_209_out, and_210_out, and_211_out,
       and_212_out, and_213_out, and_214_out, and_215_out, and_216_out, and_217_out, and_218_out,
       and_219_out, and_220_out, and_221_out, and_222_out, and_223_out, and_224_out, and_225_out,
       and_226_out, and_227_out, and_228_out, and_229_out, and_230_out, and_231_out, and_232_out,
       and_233_out, and_234_out, and_235_out, and_236_out, not_1_out, not_2_out, not_3_out, not_4_out,
       not_5_out, not_6_out, not_7_out, not_8_out, not_9_out, not_10_out, not_11_out, not_12_out, not_13_out,
       not_14_out, not_15_out, not_16_out, not_17_out, not_18_out, not_19_out, not_20_out, not_21_out,
       not_22_out, not_23_out, not_24_out, not_25_out, not_26_out, not_27_out, not_28_out, not_29_out,
       not_30_out, not_31_out, not_32_out, not_33_out, not_34_out, not_35_out, not_36_out, not_37_out,
       not_38_out, not_39_out, not_40_out, not_41_out, not_42_out, not_43_out, not_44_out, not_45_out,
       not_46_out, not_47_out, not_48_out, not_49_out, not_50_out, not_51_out, not_52_out, not_53_out,
       not_54_out, not_55_out, not_56_out, not_57_out, not_58_out, not_59_out, not_60_out, not_61_out,
       not_62_out, not_63_out, not_64_out, not_65_out, not_66_out, not_67_out, not_68_out, not_69_out,
       not_70_out, not_71_out, not_72_out, not_73_out, not_74_out, not_75_out, not_76_out, not_77_out,
       not_78_out, not_79_out, not_80_out, not_81_out, not_82_out, not_83_out, not_84_out, not_85_out,
       not_86_out, not_87_out, not_88_out, not_89_out, not_90_out, not_91_out, not_92_out, not_93_out,
       not_94_out, not_95_out, not_96_out, not_97_out, not_98_out, not_99_out, not_100_out, not_101_out,
       not_102_out, not_103_out, not_104_out, not_105_out, not_106_out, not_107_out, not_108_out,
       not_109_out, not_110_out, not_111_out, not_112_out, not_113_out, not_114_out, not_115_out,
       not_116_out, not_117_out, not_118_out, not_119_out, not_120_out, not_121_out, not_122_out,
       not_123_out, not_124_out, not_125_out, not_126_out, not_127_out, not_128_out, not_129_out,
       not_130_out, not_131_out, not_132_out, not_133_out, not_134_out, not_135_out, not_136_out,
       not_137_out, not_138_out, not_139_out, not_140_out, not_141_out, not_142_out, not_143_out,
       not_144_out, not_145_out, not_146_out, not_147_out, not_148_out, not_149_out, not_150_out,
       not_151_out, not_152_out, not_153_out, not_154_out, not_155_out, not_156_out, not_157_out,
       not_158_out, not_159_out, not_160_out, or_1_out, or_3_out, or_4_out, or_7_out, or_8_out, or_9_out,
       or_10_out, or_11_out, or_12_out, or_13_out, or_14_out, or_15_out, or_16_out, or_17_out, or_18_out,
       or_19_out, or_20_out, or_21_out, or_22_out, or_23_out, or_24_out, or_26_out, or_27_out, or_28_out,
       or_29_out, or_30_out, or_31_out, or_32_out, or_33_out, or_34_out, or_35_out, or_36_out, or_37_out,
       or_38_out, or_39_out, or_40_out, or_41_out, or_42_out, or_44_out, or_45_out, or_47_out, or_48_out,
       or_50_out, or_51_out, or_53_out;

  not not_1 (not_1_out, c);
  not not_2 (not_2_out, d);
  not not_3 (not_3_out, f);
  not not_4 (not_4_out, b);
  and and_1 (and_1_out, a, b);
  not not_5 (not_5_out, c);
  not not_6 (not_6_out, d);
  not not_7 (not_7_out, e);
  not not_8 (not_8_out, a);
  not not_9 (not_9_out, a);
  not not_10 (not_10_out, a);
  not not_11 (not_11_out, b);
  not not_12 (not_12_out, a);
  not not_13 (not_13_out, b);
  not not_14 (not_14_out, a);
  not not_15 (not_15_out, b);
  not not_16 (not_16_out, a);
  not not_17 (not_17_out, a);
  not not_18 (not_18_out, b);
  not not_19 (not_19_out, e);
  not not_20 (not_20_out, a);
  not not_21 (not_21_out, b);
  not not_22 (not_22_out, d);
  not not_23 (not_23_out, e);
  not not_24 (not_24_out, a);
  not not_25 (not_25_out, e);
  not not_26 (not_26_out, b);
  not not_27 (not_27_out, d);
  not not_28 (not_28_out, a);
  not not_29 (not_29_out, c);
  not not_30 (not_30_out, a);
  not not_31 (not_31_out, b);
  not not_32 (not_32_out, a);
  not not_33 (not_33_out, b);
  not not_34 (not_34_out, a);
  not not_35 (not_35_out, b);
  not not_36 (not_36_out, a);
  not not_37 (not_37_out, a);
  not not_38 (not_38_out, d);
  not not_39 (not_39_out, e);
  not not_40 (not_40_out, a);
  not not_41 (not_41_out, d);
  not not_42 (not_42_out, c);
  not not_43 (not_43_out, b);
  not not_44 (not_44_out, b);
  not not_45 (not_45_out, b);
  not not_46 (not_46_out, c);
  not not_47 (not_47_out, a);
  not not_48 (not_48_out, b);
  not not_49 (not_49_out, b);
  not not_50 (not_50_out, c);
  not not_51 (not_51_out, a);
  not not_52 (not_52_out, b);
  not not_53 (not_53_out, d);
  not not_54 (not_54_out, e);
  not not_55 (not_55_out, a);
  not not_56 (not_56_out, b);
  not not_57 (not_57_out, e);
  not not_58 (not_58_out, c);
  not not_59 (not_59_out, a);
  not not_60 (not_60_out, a);
  not not_61 (not_61_out, b);
  not not_62 (not_62_out, b);
  not not_63 (not_63_out, a);
  not not_64 (not_64_out, b);
  not not_65 (not_65_out, c);
  not not_66 (not_66_out, d);
  not not_67 (not_67_out, e);
  and and_2 (and_2_out, a, b);
  and and_3 (and_3_out, not_1_out, not_2_out);
  and and_4 (and_4_out, e, not_3_out);
  not not_68 (not_68_out, g);
  and and_5 (and_5_out, a, not_4_out);
  and and_6 (and_6_out, and_1_out, not_5_out);
  and and_7 (and_7_out, not_6_out, not_7_out);
  and and_8 (and_8_out, not_8_out, b);
  and and_9 (and_9_out, not_9_out, b);
  not not_69 (not_69_out, b);
  and and_10 (and_10_out, not_10_out, not_11_out);
  and and_11 (and_11_out, c, e);
  and and_12 (and_12_out, not_12_out, not_13_out);
  and and_13 (and_13_out, c, d);
  not not_70 (not_70_out, a);
  not not_71 (not_71_out, a);
  not not_72 (not_72_out, c);
  not not_73 (not_73_out, d);
  not not_74 (not_74_out, b);
  not not_75 (not_75_out, b);
  not not_76 (not_76_out, c);
  not not_77 (not_77_out, b);
  not not_78 (not_78_out, c);
  and and_14 (and_14_out, not_14_out, not_15_out);
  not not_79 (not_79_out, d);
  not not_80 (not_80_out, e);
  not not_81 (not_81_out, c);
  not not_82 (not_82_out, d);
  not not_83 (not_83_out, e);
  not not_84 (not_84_out, a);
  not not_85 (not_85_out, d);
  and and_15 (and_15_out, not_16_out, b);
  not not_86 (not_86_out, e);
  not not_87 (not_87_out, b);
  not not_88 (not_88_out, b);
  not not_89 (not_89_out, c);
  not not_90 (not_90_out, b);
  and and_16 (and_16_out, not_17_out, not_18_out);
  not not_91 (not_91_out, c);
  and and_17 (and_17_out, d, not_19_out);
  not not_92 (not_92_out, f);
  and and_18 (and_18_out, not_20_out, not_21_out);
  and and_19 (and_19_out, not_22_out, not_23_out);
  not not_93 (not_93_out, a);
  not not_94 (not_94_out, b);
  not not_95 (not_95_out, a);
  not not_96 (not_96_out, d);
  not not_97 (not_97_out, a);
  not not_98 (not_98_out, d);
  not not_99 (not_99_out, e);
  and and_20 (and_20_out, not_24_out, b);
  and and_21 (and_21_out, d, not_25_out);
  and and_22 (and_22_out, a, not_26_out);
  not not_100 (not_100_out, c);
  and and_23 (and_23_out, not_27_out, e);
  not not_101 (not_101_out, f);
  not not_102 (not_102_out, b);
  not not_103 (not_103_out, b);
  not not_104 (not_104_out, e);
  not not_105 (not_105_out, d);
  not not_106 (not_106_out, e);
  and and_24 (and_24_out, not_28_out, not_29_out);
  not not_107 (not_107_out, d);
  not not_108 (not_108_out, f);
  and and_25 (and_25_out, not_30_out, not_31_out);
  not not_109 (not_109_out, c);
  and and_26 (and_26_out, not_32_out, not_33_out);
  not not_110 (not_110_out, e);
  not not_111 (not_111_out, f);
  and and_27 (and_27_out, not_34_out, not_35_out);
  not not_112 (not_112_out, e);
  and and_28 (and_28_out, not_36_out, c);
  not not_113 (not_113_out, e);
  not not_114 (not_114_out, f);
  and and_29 (and_29_out, not_37_out, b);
  not not_115 (not_115_out, c);
  and and_30 (and_30_out, not_38_out, not_39_out);
  not not_116 (not_116_out, a);
  and and_31 (and_31_out, not_40_out, b);
  and and_32 (and_32_out, not_41_out, e);
  and and_33 (and_33_out, a, not_42_out);
  not not_117 (not_117_out, d);
  not not_118 (not_118_out, e);
  not not_119 (not_119_out, f);
  not not_120 (not_120_out, b);
  and and_34 (and_34_out, a, not_43_out);
  not not_121 (not_121_out, c);
  and and_35 (and_35_out, d, e);
  not not_122 (not_122_out, f);
  and and_36 (and_36_out, a, not_44_out);
  not not_123 (not_123_out, d);
  not not_124 (not_124_out, b);
  and and_37 (and_37_out, not_45_out, not_46_out);
  not not_125 (not_125_out, d);
  not not_126 (not_126_out, e);
  and and_38 (and_38_out, not_47_out, not_48_out);
  not not_127 (not_127_out, d);
  and and_39 (and_39_out, not_49_out, not_50_out);
  not not_128 (not_128_out, f);
  and and_40 (and_40_out, not_51_out, not_52_out);
  and and_41 (and_41_out, not_53_out, not_54_out);
  not not_129 (not_129_out, f);
  and and_42 (and_42_out, not_55_out, not_56_out);
  and and_43 (and_43_out, d, not_57_out);
  and and_44 (and_44_out, b, not_58_out);
  not not_130 (not_130_out, d);
  not not_131 (not_131_out, e);
  not not_132 (not_132_out, f);
  not not_133 (not_133_out, a);
  and and_45 (and_45_out, not_59_out, b);
  not not_134 (not_134_out, c);
  and and_46 (and_46_out, not_60_out, b);
  not not_135 (not_135_out, a);
  not not_136 (not_136_out, e);
  and and_47 (and_47_out, a, not_61_out);
  not not_137 (not_137_out, c);
  not not_138 (not_138_out, f);
  and and_48 (and_48_out, a, not_62_out);
  not not_139 (not_139_out, f);
  not not_140 (not_140_out, b);
  and and_49 (and_49_out, not_63_out, g);
  and and_50 (and_50_out, not_64_out, g);
  and and_51 (and_51_out, not_65_out, not_66_out);
  and and_52 (and_52_out, not_67_out, g);
  and and_53 (and_53_out, and_2_out, and_3_out);
  and and_54 (and_54_out, and_4_out, not_68_out);
  and and_55 (and_55_out, and_5_out, c);
  and and_56 (and_56_out, and_6_out, and_7_out);
  and and_57 (and_57_out, and_8_out, d);
  and and_58 (and_58_out, and_9_out, c);
  and and_59 (and_59_out, a, not_69_out);
  not not_141 (not_141_out, c);
  and and_60 (and_60_out, and_10_out, and_11_out);
  and and_61 (and_61_out, and_12_out, and_13_out);
  and and_62 (and_62_out, not_70_out, c);
  and and_63 (and_63_out, d, e);
  and and_64 (and_64_out, not_71_out, b);
  and and_65 (and_65_out, not_72_out, not_73_out);
  and and_66 (and_66_out, a, not_74_out);
  not not_142 (not_142_out, c);
  and and_67 (and_67_out, not_75_out, not_76_out);
  and and_68 (and_68_out, d, f);
  and and_69 (and_69_out, not_77_out, not_78_out);
  and and_70 (and_70_out, d, e);
  not not_143 (not_143_out, b);
  and and_71 (and_71_out, and_14_out, c);
  and and_72 (and_72_out, not_79_out, not_80_out);
  and and_73 (and_73_out, b, not_81_out);
  and and_74 (and_74_out, not_82_out, not_83_out);
  not not_144 (not_144_out, a);
  not not_145 (not_145_out, d);
  and and_75 (and_75_out, not_84_out, b);
  and and_76 (and_76_out, not_85_out, e);
  and and_77 (and_77_out, and_15_out, c);
  and and_78 (and_78_out, d, not_86_out);
  and and_79 (and_79_out, a, not_87_out);
  not not_146 (not_146_out, c);
  and and_80 (and_80_out, a, not_88_out);
  and and_81 (and_81_out, not_89_out, d);
  and and_82 (and_82_out, a, not_90_out);
  and and_83 (and_83_out, d, f);
  not not_147 (not_147_out, b);
  and and_84 (and_84_out, and_16_out, not_91_out);
  and and_85 (and_85_out, and_17_out, not_92_out);
  and and_86 (and_86_out, and_18_out, c);
  and and_87 (and_87_out, and_19_out, f);
  and and_88 (and_88_out, not_93_out, not_94_out);
  and and_89 (and_89_out, d, e);
  not not_148 (not_148_out, f);
  and and_90 (and_90_out, not_95_out, b);
  not not_149 (not_149_out, c);
  and and_91 (and_91_out, not_96_out, e);
  and and_92 (and_92_out, not_97_out, b);
  and and_93 (and_93_out, not_98_out, not_99_out);
  not not_150 (not_150_out, f);
  and and_94 (and_94_out, and_20_out, c);
  and and_95 (and_95_out, and_21_out, f);
  and and_96 (and_96_out, and_22_out, not_100_out);
  and and_97 (and_97_out, and_23_out, not_101_out);
  and and_98 (and_98_out, a, not_102_out);
  not not_151 (not_151_out, c);
  and and_99 (and_99_out, d, e);
  and and_100 (and_100_out, a, not_103_out);
  and and_101 (and_101_out, d, not_104_out);
  not not_152 (not_152_out, f);
  and and_102 (and_102_out, a, b);
  not not_153 (not_153_out, c);
  and and_103 (and_103_out, not_105_out, not_106_out);
  and and_104 (and_104_out, and_24_out, not_107_out);
  and and_105 (and_105_out, e, not_108_out);
  and and_106 (and_106_out, and_25_out, not_109_out);
  and and_107 (and_107_out, e, f);
  and and_108 (and_108_out, and_26_out, c);
  and and_109 (and_109_out, not_110_out, not_111_out);
  and and_110 (and_110_out, and_27_out, c);
  and and_111 (and_111_out, d, not_112_out);
  and and_112 (and_112_out, and_28_out, d);
  and and_113 (and_113_out, not_113_out, not_114_out);
  and and_114 (and_114_out, and_29_out, not_115_out);
  and and_115 (and_115_out, and_30_out, f);
  and and_116 (and_116_out, not_116_out, b);
  not not_154 (not_154_out, c);
  and and_117 (and_117_out, and_31_out, c);
  and and_118 (and_118_out, and_32_out, f);
  and and_119 (and_119_out, and_33_out, not_117_out);
  and and_120 (and_120_out, not_118_out, not_119_out);
  and and_121 (and_121_out, a, not_120_out);
  not not_155 (not_155_out, c);
  not not_156 (not_156_out, e);
  and and_122 (and_122_out, and_34_out, not_121_out);
  and and_123 (and_123_out, and_35_out, not_122_out);
  and and_124 (and_124_out, and_36_out, c);
  and and_125 (and_125_out, not_123_out, e);
  and and_126 (and_126_out, a, not_124_out);
  and and_127 (and_127_out, and_37_out, not_125_out);
  and and_128 (and_128_out, not_126_out, f);
  and and_129 (and_129_out, and_38_out, not_127_out);
  and and_130 (and_130_out, e, f);
  and and_131 (and_131_out, and_39_out, d);
  and and_132 (and_132_out, e, not_128_out);
  and and_133 (and_133_out, and_40_out, c);
  and and_134 (and_134_out, and_41_out, not_129_out);
  and and_135 (and_135_out, and_42_out, c);
  and and_136 (and_136_out, and_43_out, f);
  and and_137 (and_137_out, and_44_out, not_130_out);
  and and_138 (and_138_out, not_131_out, not_132_out);
  and and_139 (and_139_out, not_133_out, b);
  not not_157 (not_157_out, d);
  not not_158 (not_158_out, f);
  and and_140 (and_140_out, and_45_out, not_134_out);
  and and_141 (and_141_out, d, f);
  and and_142 (and_142_out, and_46_out, d);
  and and_143 (and_143_out, e, f);
  and and_144 (and_144_out, not_135_out, b);
  and and_145 (and_145_out, d, not_136_out);
  not not_159 (not_159_out, f);
  and and_146 (and_146_out, and_47_out, not_137_out);
  and and_147 (and_147_out, d, not_138_out);
  and and_148 (and_148_out, and_48_out, d);
  and and_149 (and_149_out, e, not_139_out);
  and and_150 (and_150_out, a, not_140_out);
  not not_160 (not_160_out, d);
  or or_1 (or_1_out, and_49_out, and_50_out);
  and and_151 (and_151_out, and_51_out, and_52_out);
  and and_152 (a_2, and_53_out, and_54_out);
  or or_2 (b_2, and_55_out, and_56_out);
  or or_3 (or_3_out, and_57_out, and_58_out);
  and and_153 (and_153_out, and_59_out, not_141_out);
  or or_4 (or_4_out, and_60_out, and_61_out);
  and and_154 (and_154_out, and_62_out, and_63_out);
  and and_155 (and_155_out, and_64_out, and_65_out);
  and and_156 (and_156_out, and_66_out, not_142_out);
  and and_157 (and_157_out, and_67_out, and_68_out);
  and and_158 (and_158_out, and_69_out, and_70_out);
  and and_159 (and_159_out, not_143_out, d);
  and and_160 (and_160_out, e, f);
  and and_161 (and_161_out, and_71_out, and_72_out);
  and and_162 (and_162_out, and_73_out, and_74_out);
  and and_163 (and_163_out, not_144_out, b);
  and and_164 (and_164_out, not_145_out, f);
  and and_165 (and_165_out, and_75_out, and_76_out);
  and and_166 (and_166_out, and_77_out, and_78_out);
  and and_167 (and_167_out, and_79_out, not_146_out);
  and and_168 (and_168_out, e, f);
  and and_169 (and_169_out, and_80_out, and_81_out);
  and and_170 (and_170_out, and_82_out, and_83_out);
  and and_171 (and_171_out, a, not_147_out);
  and and_172 (and_172_out, d, e);
  and and_173 (and_173_out, and_84_out, and_85_out);
  and and_174 (and_174_out, and_86_out, and_87_out);
  and and_175 (and_175_out, and_88_out, c);
  and and_176 (and_176_out, and_89_out, not_148_out);
  and and_177 (and_177_out, and_90_out, not_149_out);
  and and_178 (and_178_out, and_91_out, f);
  and and_179 (and_179_out, and_92_out, c);
  and and_180 (and_180_out, and_93_out, not_150_out);
  and and_181 (and_181_out, and_94_out, and_95_out);
  and and_182 (and_182_out, and_96_out, and_97_out);
  and and_183 (and_183_out, and_98_out, not_151_out);
  and and_184 (and_184_out, and_99_out, f);
  and and_185 (and_185_out, and_100_out, c);
  and and_186 (and_186_out, and_101_out, not_152_out);
  and and_187 (and_187_out, and_102_out, not_153_out);
  and and_188 (and_188_out, and_103_out, f);
  and and_189 (and_189_out, and_104_out, and_105_out);
  and and_190 (and_190_out, and_106_out, and_107_out);
  and and_191 (and_191_out, and_108_out, and_109_out);
  and and_192 (and_192_out, and_110_out, and_111_out);
  and and_193 (and_193_out, and_112_out, and_113_out);
  and and_194 (and_194_out, and_114_out, and_115_out);
  and and_195 (and_195_out, and_116_out, not_154_out);
  and and_196 (and_196_out, d, e);
  and and_197 (and_197_out, and_117_out, and_118_out);
  and and_198 (and_198_out, and_119_out, and_120_out);
  and and_199 (and_199_out, and_121_out, not_155_out);
  and and_200 (and_200_out, not_156_out, f);
  and and_201 (and_201_out, and_122_out, and_123_out);
  and and_202 (and_202_out, and_124_out, and_125_out);
  and and_203 (and_203_out, and_126_out, c);
  and and_204 (and_204_out, e, f);
  and and_205 (and_205_out, and_127_out, and_128_out);
  and and_206 (and_206_out, and_129_out, and_130_out);
  and and_207 (and_207_out, and_131_out, and_132_out);
  and and_208 (and_208_out, and_133_out, and_134_out);
  and and_209 (and_209_out, and_135_out, and_136_out);
  and and_210 (and_210_out, and_137_out, and_138_out);
  and and_211 (and_211_out, and_139_out, not_157_out);
  and and_212 (and_212_out, e, not_158_out);
  and and_213 (and_213_out, and_140_out, and_141_out);
  and and_214 (and_214_out, and_142_out, and_143_out);
  and and_215 (and_215_out, and_144_out, c);
  and and_216 (and_216_out, and_145_out, not_159_out);
  and and_217 (and_217_out, and_146_out, and_147_out);
  and and_218 (and_218_out, and_148_out, and_149_out);
  and and_219 (and_219_out, and_150_out, c);
  and and_220 (and_220_out, not_160_out, f);
  or or_5 (i, or_1_out, and_151_out);
  or or_6 (c_2, or_3_out, and_153_out);
  or or_7 (or_7_out, or_4_out, and_154_out);
  or or_8 (or_8_out, and_155_out, and_156_out);
  or or_9 (or_9_out, and_157_out, and_158_out);
  and and_221 (and_221_out, and_159_out, and_160_out);
  or or_10 (or_10_out, and_161_out, and_162_out);
  and and_222 (and_222_out, and_163_out, and_164_out);
  or or_11 (or_11_out, and_165_out, and_166_out);
  and and_223 (and_223_out, and_167_out, and_168_out);
  or or_12 (or_12_out, and_169_out, and_170_out);
  and and_224 (and_224_out, and_171_out, and_172_out);
  or or_13 (or_13_out, and_173_out, and_174_out);
  and and_225 (and_225_out, and_175_out, and_176_out);
  and and_226 (and_226_out, and_177_out, and_178_out);
  and and_227 (and_227_out, and_179_out, and_180_out);
  or or_14 (or_14_out, and_181_out, and_182_out);
  and and_228 (and_228_out, and_183_out, and_184_out);
  and and_229 (and_229_out, and_185_out, and_186_out);
  and and_230 (and_230_out, and_187_out, and_188_out);
  or or_15 (or_15_out, and_189_out, and_190_out);
  or or_16 (or_16_out, and_191_out, and_192_out);
  or or_17 (or_17_out, and_193_out, and_194_out);
  and and_231 (and_231_out, and_195_out, and_196_out);
  or or_18 (or_18_out, and_197_out, and_198_out);
  and and_232 (and_232_out, and_199_out, and_200_out);
  or or_19 (or_19_out, and_201_out, and_202_out);
  and and_233 (and_233_out, and_203_out, and_204_out);
  or or_20 (or_20_out, and_205_out, and_206_out);
  or or_21 (or_21_out, and_207_out, and_208_out);
  or or_22 (or_22_out, and_209_out, and_210_out);
  and and_234 (and_234_out, and_211_out, and_212_out);
  or or_23 (or_23_out, and_213_out, and_214_out);
  and and_235 (and_235_out, and_215_out, and_216_out);
  or or_24 (or_24_out, and_217_out, and_218_out);
  and and_236 (and_236_out, and_219_out, and_220_out);
  or or_25 (d_2, or_7_out, or_8_out);
  or or_26 (or_26_out, or_9_out, and_221_out);
  or or_27 (or_27_out, or_10_out, and_222_out);
  or or_28 (or_28_out, or_11_out, and_223_out);
  or or_29 (or_29_out, or_12_out, and_224_out);
  or or_30 (or_30_out, or_13_out, and_225_out);
  or or_31 (or_31_out, and_226_out, and_227_out);
  or or_32 (or_32_out, or_14_out, and_228_out);
  or or_33 (or_33_out, and_229_out, and_230_out);
  or or_34 (or_34_out, or_15_out, or_16_out);
  or or_35 (or_35_out, or_17_out, and_231_out);
  or or_36 (or_36_out, or_18_out, and_232_out);
  or or_37 (or_37_out, or_19_out, and_233_out);
  or or_38 (or_38_out, or_20_out, or_21_out);
  or or_39 (or_39_out, or_22_out, and_234_out);
  or or_40 (or_40_out, or_23_out, and_235_out);
  or or_41 (or_41_out, or_24_out, and_236_out);
  or or_42 (or_42_out, or_26_out, or_27_out);
  or or_43 (e_2, or_42_out, or_44_out);
  or or_44 (or_44_out, or_28_out, or_29_out);
  or or_45 (or_45_out, or_30_out, or_31_out);
  or or_46 (f_2, or_45_out, or_47_out);
  or or_47 (or_47_out, or_32_out, or_33_out);
  or or_48 (or_48_out, or_34_out, or_35_out);
  or or_49 (g_2, or_48_out, or_50_out);
  or or_50 (or_50_out, or_36_out, or_37_out);
  or or_51 (or_51_out, or_38_out, or_39_out);
  or or_52 (h, or_51_out, or_53_out);
  or or_53 (or_53_out, or_40_out, or_41_out);
endmodule
