// Logisim project UP-DOWN 5-bit Mod N Counter.circ as structural Verilog: 2 circuits, main circuit 1
module _1 (
  input  in_1,
  input  input_N,
  input  in_3,
  input  in_4,
  input  in_5
);

  wire ckt_1__1___up, ckt_1_b1, ckt_1_b2, ckt_1_b3, ckt_1_lsb, ckt_1_msb, mode_toggle_out;

  Button mode_toggle (.out(mode_toggle_out));
  LED led_1 (.in(ckt_1__1___up));
  ckt ckt_1 (
    ._0__down(mode_toggle_out), ._1___up(ckt_1__1___up), .in_1(in_1), .in_2(input_N), .in_3(in_3),
    .in_4(in_4), .in_5(in_5), .msb(ckt_1_msb), .b3(ckt_1_b3), .b2(ckt_1_b2), .b1(ckt_1_b1), .lsb(ckt_1_lsb));
  LED led_2 (.in(ckt_1_b1));
  LED led_3 (.in(ckt_1_b3));
  LED led_4 (.in(ckt_1_b2));
  LED led_5 (.in(ckt_1_msb));
  LED led_6 (.in(ckt_1_lsb));

  // Notes on the sheet:
  //   Bruce Oliver B. Apos
  //   EE 160 ST-1L
  //   May 7, 2019
  //   reference: https://www.electronics-tutorials.ws/counter/count_4.html
  //   UP-DOWN 5-bit Mod-N counter
  //   on - up counter
  //   off - down counter
  //   output
endmodule

module ckt (
  input  in_1,
  input  in_2,
  input  in_3,
  input  in_4,
  input  in_5,
  input  _0__down,
  output msb,
  output b3,
  output b2,
  output b1,
  output lsb,
  output _1___up
);

  wire and_1_out, and_2_out, and_4_out, and_5_out, and_6_out, and_7_out, and_8_out, and_9_out, clock_1_out,
       j_k_ff_1_qn, j_k_ff_2_qn, j_k_ff_3_qn, j_k_ff_4_qn, multiplexer_1_out, multiplexer_2_out,
       multiplexer_3_out, multiplexer_4_out, multiplexer_5_out, multiplexer_6_out, multiplexer_7_out,
       nor_1_out, not_1_out, or_1_out, or_2_out, or_3_out, or_4_out, up_reset, xnor_1_out, xnor_2_out,
       xnor_3_out, xnor_4_out, xnor_5_out;

  Clock clock_1 (.out(clock_1_out));
  T_Flip_Flop t_ff_1 (.clk(_0__down), .T(_0__down), .Q(_1___up));  // open: Qn, preset, reset, en
  J_K_Flip_Flop j_k_ff_1 (
    .J(1'b1), .clk(clock_1_out), .K(1'b1), .Q(lsb), .Qn(j_k_ff_1_qn), .preset(multiplexer_1_out),
    .reset(multiplexer_6_out));  // open: en
  not not_1 (not_1_out, _1___up);
  Multiplexer #(.enable("false")) multiplexer_1 (
    .in0(1'b0), .in1(in_5), .out(multiplexer_1_out), .sel(multiplexer_7_out));
  and and_1 (and_1_out, _1___up, lsb);
  or or_1 (or_1_out, and_1_out, and_2_out);
  and and_2 (and_2_out, j_k_ff_1_qn, not_1_out);
  xnor xnor_1 (xnor_1_out, in_5, lsb);
  xnor xnor_2 (xnor_2_out, in_4, b1);
  xnor xnor_3 (xnor_3_out, in_3, b2);
  xnor xnor_4 (xnor_4_out, in_2, b3);
  xnor xnor_5 (xnor_5_out, in_1, msb);
  J_K_Flip_Flop j_k_ff_2 (
    .J(or_1_out), .clk(clock_1_out), .K(or_1_out), .Q(b1), .Qn(j_k_ff_2_qn), .preset(multiplexer_2_out),
    .reset(multiplexer_6_out));  // open: en
  Multiplexer #(.enable("false")) multiplexer_2 (
    .in0(1'b0), .in1(in_4), .out(multiplexer_2_out), .sel(multiplexer_7_out));
  and and_3 (up_reset, xnor_1_out, xnor_2_out, xnor_3_out, xnor_4_out, xnor_5_out);
  and and_4 (and_4_out, and_1_out, b1);
  or or_2 (or_2_out, and_4_out, and_5_out);
  and and_5 (and_5_out, j_k_ff_2_qn, and_2_out);
  J_K_Flip_Flop j_k_ff_3 (
    .J(or_2_out), .clk(clock_1_out), .K(or_2_out), .Q(b2), .Qn(j_k_ff_3_qn), .preset(multiplexer_3_out),
    .reset(multiplexer_6_out));  // open: en
  Multiplexer #(.enable("false")) multiplexer_3 (
    .in0(1'b0), .in1(in_3), .out(multiplexer_3_out), .sel(multiplexer_7_out));
  and and_6 (and_6_out, and_4_out, b2);
  or or_3 (or_3_out, and_6_out, and_7_out);
  and and_7 (and_7_out, j_k_ff_3_qn, and_5_out);
  J_K_Flip_Flop j_k_ff_4 (
    .J(or_3_out), .clk(clock_1_out), .K(or_3_out), .Q(b3), .Qn(j_k_ff_4_qn), .preset(multiplexer_4_out),
    .reset(multiplexer_6_out));  // open: en
  Multiplexer #(.enable("false")) multiplexer_4 (
    .in0(1'b0), .in1(in_2), .out(multiplexer_4_out), .sel(multiplexer_7_out));
  and and_8 (and_8_out, and_6_out, b3);
  or or_4 (or_4_out, and_8_out, and_9_out);
  and and_9 (and_9_out, j_k_ff_4_qn, and_7_out);
  J_K_Flip_Flop j_k_ff_5 (
    .J(or_4_out), .clk(clock_1_out), .K(or_4_out), .Q(msb), .preset(multiplexer_5_out),
    .reset(multiplexer_6_out));  // open: Qn, en
  Multiplexer #(.enable("false")) multiplexer_5 (
    .in0(1'b0), .in1(in_1), .out(multiplexer_5_out), .sel(multiplexer_7_out));
  Multiplexer #(.enable("false")) multiplexer_6 (.in0(1'b0), .in1(up_reset), .out(multiplexer_6_out), .sel(_1___up));
  nor nor_1 (nor_1_out, msb, b3, b2, b1, lsb);
  Multiplexer #(.enable("false")) multiplexer_7 (.in0(nor_1_out), .in1(1'b0), .out(multiplexer_7_out), .sel(_1___up));

  // Other names for the same wires on the sheet: b1_t = in_4; b2_t = in_3; b3_t = in_2; lsb_t = in_5; m = _1___up;
  //   msb_t = in_1

  // Notes on the sheet:
  //   XNOR checks if N is equal to Q out
  //   AND allows reset if all bits are the same as Q out
  //   allows for reset once in up mode
  //   check if counter reached 00000
  //   allows for reset once in down mode
endmodule
