// Logisim project Universal Shift Register.circ as structural Verilog: 3 circuits, main circuit USR
module USR (
  input  in_1,
  input  in_2,
  input  in_3,
  input  in_4,
  input  shift_input,
  input  right_sh__mode_toggle,
  input  left_sh__mode_toggle
);

  wire clear_out, n4_ff_1_out_12, n4_ff_1_out_14, n4_ff_1_out_15, n4_ff_1_output, parallel_loading_out,
       shift_left_out, shift_right_out;

  Button clear (.out(clear_out));
  Button shift_right (.out(shift_right_out));
  Button shift_left (.out(shift_left_out));
  Button parallel_loading (.out(parallel_loading_out));
  LED led_1 (.in(n4_ff_1_output));
  LED led_2 (.in(n4_ff_1_out_12));
  _4_FF u_4_ff_1 (
    .clear(clear_out), .shift_input(shift_input), .shift_right(shift_right_out), .shift_left(shift_left_out),
    .parallel_loading(parallel_loading_out), .in_1(in_1), .in_2(in_2), .in_3(in_3), .in_4(in_4),
    .out_12(n4_ff_1_out_12), .\output (n4_ff_1_output), .out_14(n4_ff_1_out_14), .out_15(n4_ff_1_out_15),
    .in_10(right_sh__mode_toggle), .in_11(left_sh__mode_toggle));
  LED led_3 (.in(n4_ff_1_out_14));
  LED led_4 (.in(n4_ff_1_out_15));

  // Notes on the sheet:
  //   Bruce Oliver Apos
  //   EE 160 ST 1L
  //   Universal Shift Register
  //   parallel loading input
  //   output
  //   Reference: Universal Shift Register by Neso Academy (https://www.youtube.com/watch?v=AEGzpMlOsvc)
  //   Machine Problem 1
  //   0-input mode
  //   1-ring mode
endmodule

module _4_FF (
  input  in_1,
  input  in_2,
  input  in_3,
  input  in_4,
  input  clear,
  input  shift_input,
  input  shift_right,
  input  shift_left,
  input  parallel_loading,
  input  in_10,
  input  in_11,
  output out_12,
  output \output ,
  output out_14,
  output out_15
);

  wire inputs_1_to_clock_pulse, multiplexer_1_out, multiplexer_2_out, multiplexer_3_out, multiplexer_4_out,
       multiplexer_5_out, multiplexer_6_out;
  wire [1:0] inputs_1_selector_out;

  inputs inputs_1 (
    .shift_right(shift_right), .shift_left(shift_left), .parallel_load(parallel_loading),
    .to_clock_pulse(inputs_1_to_clock_pulse), .selector_out(inputs_1_selector_out));
  Multiplexer #(.select(2), .enable("false")) multiplexer_1 (
    .in1(multiplexer_5_out), .in2(\output ), .in3(in_1), .out(multiplexer_1_out), .sel(inputs_1_selector_out));  // open: in0
  D_Flip_Flop d_ff_1 (
    .clk(inputs_1_to_clock_pulse), .D(multiplexer_1_out), .Q(out_12), .reset(clear));  // open: Qn, preset, en
  Multiplexer #(.select(2), .enable("false")) multiplexer_2 (
    .in1(out_12), .in2(out_14), .in3(in_2), .out(multiplexer_2_out), .sel(inputs_1_selector_out));  // open: in0
  D_Flip_Flop d_ff_2 (
    .clk(inputs_1_to_clock_pulse), .D(multiplexer_2_out), .Q(\output ), .reset(clear));  // open: Qn, preset, en
  Multiplexer #(.select(2), .enable("false")) multiplexer_3 (
    .in1(\output ), .in2(out_15), .in3(in_3), .out(multiplexer_3_out), .sel(inputs_1_selector_out));  // open: in0
  D_Flip_Flop d_ff_3 (
    .clk(inputs_1_to_clock_pulse), .D(multiplexer_3_out), .Q(out_14), .reset(clear));  // open: Qn, preset, en
  Multiplexer #(.select(2), .enable("false")) multiplexer_4 (
    .in1(out_14), .in2(multiplexer_6_out), .in3(in_4), .out(multiplexer_4_out), .sel(inputs_1_selector_out));  // open: in0
  D_Flip_Flop d_ff_4 (
    .clk(inputs_1_to_clock_pulse), .D(multiplexer_4_out), .Q(out_15), .reset(clear));  // open: Qn, preset, en
  Multiplexer #(.enable("false")) multiplexer_5 (.in0(shift_input), .in1(out_15), .out(multiplexer_5_out), .sel(in_10));
  Multiplexer #(.enable("false")) multiplexer_6 (.in0(shift_input), .in1(out_12), .out(multiplexer_6_out), .sel(in_11));

  // Notes on the sheet:
  //   input module
  //   Select switch for MUX:
  //   01-shift right
  //   10-shift left
  //   11-parallel load
  //   Each 2-bit MUX are connected to the D-inputs of the D FFs.
  //   The inputs of the MUX are configured to the functions shift, and parallel load.
  //   parallel loading input
  //   shift modes
endmodule

module inputs (
  input  shift_right,
  input  shift_left,
  input  parallel_load,
  output to_clock_pulse,
  output [1:0] selector_out
);

  wire d_ff_1_q, d_ff_2_q, d_ff_3_q, or_1_out, or_2_out, or_3_out, or_4_out;
  wire [1:0] multiplexer_1_out, multiplexer_2_out, multiplexer_3_out;

  or or_1 (or_1_out, shift_right, shift_left, parallel_load);
  not not_1 (to_clock_pulse, or_1_out);
  D_Flip_Flop d_ff_1 (.clk(shift_right), .D(shift_right), .Q(d_ff_1_q), .reset(or_2_out));  // open: Qn, preset, en
  or or_2 (or_2_out, parallel_load, shift_left);
  D_Flip_Flop d_ff_2 (.clk(shift_left), .D(shift_left), .Q(d_ff_2_q), .reset(or_3_out));  // open: Qn, preset, en
  or or_3 (or_3_out, parallel_load, shift_right);
  D_Flip_Flop d_ff_3 (.clk(parallel_load), .D(parallel_load), .Q(d_ff_3_q), .reset(or_4_out));  // open: Qn, preset, en
  or or_4 (or_4_out, shift_right, shift_left);
  Multiplexer #(.width(2), .enable("false")) multiplexer_1 (
    .in0(2'b00), .in1(2'b01), .out(multiplexer_1_out), .sel(d_ff_1_q));
  Multiplexer #(.width(2), .enable("false")) multiplexer_2 (
    .in0(2'b00), .in1(2'b10), .out(multiplexer_2_out), .sel(d_ff_2_q));
  Multiplexer #(.width(2), .enable("false")) multiplexer_3 (
    .in0(2'b00), .in1(2'b11), .out(multiplexer_3_out), .sel(d_ff_3_q));
  assign selector_out = multiplexer_1_out | multiplexer_2_out | multiplexer_3_out;  // OR_Gate or_5, 2 bits wide

  // Notes on the sheet:
  //   (01)
  //   (10)
  //   (11)
  //   when modes are clicked, clock pulse is triggered
  //   D FFs are used as latch to hold the selector for each MUX
endmodule
